# Fritzing sketch wild_mini_4wd (saved by Fritzing 0.9.2b)

parts:
  JP2 = DRV8830 [package=self]
  ESP1 = ESP32-DevkitC
  J1 = Basic Servo
  VCC1 = 4 x AAA Battery Mount  # not connected
  M1 = DC Motor  # not connected

nets:
  VCC: JP2.VCC, ESP1.3V3
  GND: JP2.GND, ESP1.GND
  N1: JP2.SDA, ESP1.IO21
  N2: JP2.SCL, ESP1.IO22
  N3: ESP1.IO13, J1.pulse
